# Fritzing sketch MainCircuit (saved by Fritzing 0.9.3b)

parts:
  M1 = fc-51 [package=THT]
  M2 = fc-51 [package=THT]
  M3 = fc-51 [package=THT]
  Part1 = Arduino Uno (Rev3) - ICSP
  M4 = L293D Motor Driver
  VCC1 = Battery block 9V  # not connected
  M6 = DC Motor  # not connected
  M7 = DC Motor  # not connected

nets:
  N1: M1.pin1, Part1.D5_PWM
  N2: M1.pin2, M2.pin2, M3.pin2, Part1.GND
  N3: M1.pin3, M2.pin3, M3.pin3, Part1.5V
  N4: M2.pin1, Part1.D3_PWM
  N5: M3.pin1, Part1.D4
  N6: Part1.D8, M4.pin_8
  N7: Part1.D9_PWM, M4.pin_7
  N8: Part1.D10_PWM/SS, M4.pin_6
  N9: Part1.D11_PWM/MOSI, M4.pin_5
